// Logisim project 8bit-CPU.circ as structural Verilog: 5 circuits, main circuit main
module main (
  input  rst,
  input  hlt,
  output [7:0] out_3
);

  wire clock_1_out, cpu_1_wr_mem, not_1_out;
  wire [3:0] cpu_1_mem_addr;
  wire [7:0] bit_extender_1_out, cpu_1_pc, cpu_1_wdata, ram_1_data, rom_1_data;

  Clock clock_1 (.out(clock_1_out));
  assign bit_extender_1_out = {{4{1'b0}}, cpu_1_mem_addr};  // Bit_Extender bit_extender_1
  not not_1 (not_1_out, cpu_1_wr_mem);
  RAM #(.bus("separate")) ram_1 (
    .addr(bit_extender_1_out), .din(cpu_1_wdata), .data(ram_1_data), .str(cpu_1_wr_mem), .clk(clock_1_out),
    .ld(not_1_out));  // open: sel, clr
  CPU cpu_1 (
    .inst(rom_1_data), .clk(clock_1_out), .rst(rst), .hlt(hlt), .\output (out_3), .pc(cpu_1_pc),
    .mem_addr(cpu_1_mem_addr), .rdata(ram_1_data), .wdata(cpu_1_wdata), .wr_mem(cpu_1_wr_mem));
  Hex_Digit_Display hex_digit_display_1 (.value(out_3[7:4]));  // open: dp
  Hex_Digit_Display hex_digit_display_2 (.value(out_3[3:0]));  // open: dp
  ROM rom_1 (.addr(cpu_1_pc), .data(rom_1_data));  // open: sel

  // Notes on the sheet:
  //   SAP-1
  //   contents of rom_1 (hex, n*v repeats v):
  //   4b 30 40 31 41 32 33 1 12 31 e0 2 13 32 20 77 1 e0 f0
endmodule

module ALU (
  input  [7:0] A,
  input  [7:0] B,
  input  clk,
  input  [3:0] op,
  output [7:0] S,
  output Z,
  output C,
  output wr
);

  wire adder_1_cout, multiplexer_2_out, multiplexer_4_out, multiplexer_5_out, multiplexer_6_out, not_1_out,
       or_1_out, subtractor_1_bout;
  wire [7:0] adder_1_out, subtractor_1_out;

  Adder adder_1 (.a(A), .b(B), .out(adder_1_out), .cin(1'b0), .cout(adder_1_cout));
  Subtractor subtractor_1 (.a(A), .b(B), .out(subtractor_1_out), .bin(1'b0), .bout(subtractor_1_bout));
  Multiplexer #(.select(4), .width(8), .enable("false")) multiplexer_1 (
    .in0(B), .in1(adder_1_out), .in2(subtractor_1_out), .in3(A), .in4(B), .in5(A), .in6(A), .in7(A), .in8(A),
    .in9(A), .in10(A), .in11(A), .in12(A), .in13(A), .in14(A), .in15(A), .out(S), .sel(op));
  Multiplexer #(.select(4), .enable("false")) multiplexer_2 (
    .in0(1'b0), .in1(adder_1_cout), .in2(subtractor_1_bout), .in3(1'b0), .in4(1'b0), .in5(1'b0), .in6(1'b0),
    .in7(1'b0), .in8(1'b0), .in9(1'b0), .in10(1'b0), .in11(1'b0), .in12(1'b0), .in13(1'b0), .in14(1'b0),
    .in15(1'b0), .out(multiplexer_2_out), .sel(op));
  Multiplexer #(.select(4), .enable("false")) multiplexer_3 (
    .in0(1'b1), .in1(1'b1), .in2(1'b1), .in3(1'b0), .in4(1'b1), .in5(1'b0), .in6(1'b0), .in7(1'b0),
    .in8(1'b0), .in9(1'b0), .in10(1'b0), .in11(1'b0), .in12(1'b0), .in13(1'b0), .in14(1'b0), .in15(1'b0),
    .out(wr), .sel(op));
  or or_1 (or_1_out, S[0], S[1], S[2], S[3], S[4], S[5], S[6], S[7]);
  Multiplexer #(.select(4), .enable("false")) multiplexer_4 (
    .in0(1'b0), .in1(1'b1), .in2(1'b1), .in3(1'b0), .in4(1'b0), .in5(1'b0), .in6(1'b0), .in7(1'b0),
    .in8(1'b0), .in9(1'b0), .in10(1'b0), .in11(1'b0), .in12(1'b0), .in13(1'b0), .in14(1'b0), .in15(1'b0),
    .out(multiplexer_4_out), .sel(op));
  not not_1 (not_1_out, or_1_out);
  Multiplexer #(.enable("false")) multiplexer_5 (
    .in0(Z), .in1(not_1_out), .out(multiplexer_5_out), .sel(multiplexer_4_out));
  Multiplexer #(.enable("false")) multiplexer_6 (
    .in0(C), .in1(multiplexer_2_out), .out(multiplexer_6_out), .sel(multiplexer_4_out));
  D_Flip_Flop d_ff_1 (.clk(clk), .D(multiplexer_5_out), .Q(Z));  // open: Qn, preset, en, reset
  D_Flip_Flop d_ff_2 (.clk(clk), .D(multiplexer_6_out), .Q(C));  // open: Qn, preset, en, reset
endmodule

module CPU (
  input  [7:0] inst,
  input  clk,
  input  rst,
  input  hlt,
  input  [7:0] rdata,
  output [7:0] \output ,
  output [7:0] pc,
  output [3:0] mem_addr,
  output [7:0] wdata,
  output wr_mem
);

  wire alu_1_c, alu_1_wr, alu_1_z, and_1_out, and_2_out, and_3_out, demultiplexer_1_out4,
       demultiplexer_1_out5, demultiplexer_1_out6, demultiplexer_1_out7, demultiplexer_1_out14,
       demultiplexer_1_out15, not_1_out, not_2_out, or_1_out, or_2_out;
  wire [3:0] if_1_op;
  wire [7:0] alu_1_s, bit_extender_1_out, bit_extender_2_out, multiplexer_1_out, multiplexer_2_out,
       multiplexer_3_out;

  Multiplexer #(.width(8), .enable("false")) multiplexer_1 (
    .in0(wdata), .in1(alu_1_s), .out(multiplexer_1_out), .sel(alu_1_wr));
  or or_1 (or_1_out, demultiplexer_1_out15, hlt);
  IF if_1 (.inst(inst), .addr(mem_addr), .op(if_1_op));
  Register Reg (.D(multiplexer_1_out), .en(not_1_out), .Q(wdata), .clk(clk), .clr(rst));
  not not_1 (not_1_out, or_1_out);
  assign bit_extender_1_out = {{4{1'b0}}, mem_addr};  // Bit_Extender bit_extender_1
  Multiplexer #(.width(8), .enable("false")) multiplexer_2 (
    .in0(rdata), .in1(bit_extender_1_out), .out(multiplexer_2_out), .sel(demultiplexer_1_out4));
  ALU alu_1 (
    .A(wdata), .B(multiplexer_2_out), .op(if_1_op), .S(alu_1_s), .wr(alu_1_wr), .C(alu_1_c), .Z(alu_1_z),
    .clk(clk));
  Demultiplexer #(.select(4), .enable("false")) demultiplexer_1 (
    .out3(wr_mem), .out4(demultiplexer_1_out4), .out5(demultiplexer_1_out5), .out6(demultiplexer_1_out6),
    .out7(demultiplexer_1_out7), .out14(demultiplexer_1_out14), .out15(demultiplexer_1_out15), .in(1'b1),
    .sel(if_1_op));  // open: out0, out1, out2, out8, out9, out10, out11, out12, out13
  and and_1 (and_1_out, demultiplexer_1_out6, alu_1_z);
  and and_2 (and_2_out, demultiplexer_1_out7, alu_1_c);
  not not_2 (not_2_out, or_2_out);
  or or_2 (or_2_out, demultiplexer_1_out5, and_1_out, and_2_out);
  and and_3 (and_3_out, not_2_out, not_1_out);
  Counter Counter (
    .load(or_2_out), .D(bit_extender_2_out), .count(and_3_out), .Q(pc), .clk(clk), .clr(rst));  // open: carry
  assign bit_extender_2_out = {{4{1'b0}}, mem_addr};  // Bit_Extender bit_extender_2
  Register register_1 (.D(multiplexer_3_out), .Q(\output ), .clk(clk), .clr(rst));  // open: en
  Multiplexer #(.width(8), .enable("false")) multiplexer_3 (
    .in0(\output ), .in1(wdata), .out(multiplexer_3_out), .sel(demultiplexer_1_out14));
endmodule

module IF (
  input  [7:0] inst,
  output [3:0] addr,
  output [3:0] op
);


  assign addr = inst[3:0];
  assign op = inst[7:4];
endmodule

// HLT
module HALT (
  input  [3:0] op,
  output halt
);

  and and_1 (halt, op[0], op[1], op[2], op[3]);
endmodule
